// Logisim project SAP1 1607048.circ as structural Verilog: 5 circuits, main circuit main
module main (
  input  [3:0] HIGH,
  input  [3:0] LOW
);

  wire [7:0] register_8_bit_1_y0;

  Register_8_bit register_8_bit_1 (
    .X7(HIGH[3]), .X6(HIGH[2]), .X5(HIGH[1]), .X4(HIGH[0]), .X3(LOW[3]), .X2(LOW[2]), .X1(LOW[1]),
    .X0(LOW[0]), .Y7(register_8_bit_1_y0[7]), .Y6(register_8_bit_1_y0[6]), .Y5(register_8_bit_1_y0[5]),
    .Y4(register_8_bit_1_y0[4]), .Y3(register_8_bit_1_y0[3]), .Y2(register_8_bit_1_y0[2]),
    .Y1(register_8_bit_1_y0[1]), .Y0(register_8_bit_1_y0[0]));  // open: LOAD, CLK, CLR, ENABLE
  ALU alu_1 ();  // open: X, Y, Cin, S, Cout

  // Notes on the sheet:
  //   Roll: 1607048
  //   Name: Faisal Ahmed
endmodule

module FA (
  input  X,
  input  Y,
  input  Z,
  output S,
  output C
);

  wire AND_1_out, AND_2_out, XOR_1_out;

  xor XOR_1 (XOR_1_out, X, Y);
  and AND_1 (AND_1_out, X, Y);
  xor XOR_2 (S, XOR_1_out, Z);
  and AND_2 (AND_2_out, Z, XOR_1_out);
  or OR (C, AND_2_out, AND_1_out);

  // Notes on the sheet:
  //   Name: Faisal Ahmed
  //   Roll: 1607048
endmodule

module Register_4_bit (
  input  X3,
  input  X2,
  input  X1,
  input  X0,
  input  LOAD,
  input  CLK,
  input  CLR,
  input  ENABLE,
  output Y3,
  output Y2,
  output Y1,
  output Y0
);

  wire and_1_out, and_2_out, and_3_out, and_4_out, and_5_out, and_6_out, and_7_out, and_8_out, d_ff_1_q,
       d_ff_2_q, d_ff_3_q, d_ff_4_q, not_1_out, or_1_out, or_2_out, or_3_out, or_4_out;

  and and_1 (and_1_out, d_ff_1_q, not_1_out);
  and and_2 (and_2_out, X3, LOAD);
  or or_1 (or_1_out, and_1_out, and_2_out);
  D_Flip_Flop d_ff_1 (.clk(CLK), .D(or_1_out), .Q(d_ff_1_q), .reset(CLR));  // open: Qn, preset, en
  assign Y3 = ENABLE ? d_ff_1_q : 1'bz;  // Controlled_Buffer controlled_buffer_1
  and and_3 (and_3_out, d_ff_2_q, not_1_out);
  or or_2 (or_2_out, and_3_out, and_4_out);
  and and_4 (and_4_out, X2, LOAD);
  D_Flip_Flop d_ff_2 (.clk(CLK), .D(or_2_out), .Q(d_ff_2_q), .reset(CLR));  // open: Qn, preset, en
  assign Y2 = ENABLE ? d_ff_2_q : 1'bz;  // Controlled_Buffer controlled_buffer_2
  buf and_5 (and_5_out, d_ff_3_q);  // AND_Gate
  or or_3 (or_3_out, and_5_out, and_6_out);
  and and_6 (and_6_out, X1, LOAD);
  D_Flip_Flop d_ff_3 (.clk(CLK), .D(or_3_out), .Q(d_ff_3_q), .reset(CLR));  // open: Qn, preset, en
  and and_7 (and_7_out, d_ff_4_q, not_1_out);
  assign Y1 = ENABLE ? d_ff_3_q : 1'bz;  // Controlled_Buffer controlled_buffer_3
  not not_1 (not_1_out, LOAD);
  and and_8 (and_8_out, X0, LOAD);
  or or_4 (or_4_out, and_7_out, and_8_out);
  D_Flip_Flop d_ff_4 (.clk(CLK), .D(or_4_out), .Q(d_ff_4_q), .reset(CLR));  // open: Qn, preset, en
  assign Y0 = ENABLE ? d_ff_4_q : 1'bz;  // Controlled_Buffer controlled_buffer_4

  // Notes on the sheet:
  //   Roll:1607048
endmodule

// A
module Register_8_bit (
  input  X3,
  input  X2,
  input  X1,
  input  X0,
  input  X7,
  input  X6,
  input  X5,
  input  X4,
  input  LOAD,
  input  CLK,
  input  CLR,
  input  ENABLE,
  output Y3,
  output Y2,
  output Y1,
  output Y0,
  output Y5,
  output Y4,
  output Y7,
  output Y6
);

  wire and_1_out, and_2_out, and_3_out, and_4_out, and_5_out, and_6_out, and_7_out, and_8_out, and_9_out,
       and_10_out, and_11_out, and_12_out, and_13_out, and_14_out, and_15_out, and_16_out, d_ff_1_q,
       d_ff_2_q, d_ff_3_q, d_ff_4_q, d_ff_5_q, d_ff_6_q, d_ff_7_q, d_ff_8_q, not_1_out, or_1_out, or_2_out,
       or_3_out, or_4_out, or_5_out, or_6_out, or_7_out, or_8_out;

  and and_1 (and_1_out, X7, LOAD);
  and and_2 (and_2_out, d_ff_1_q, not_1_out);
  or or_1 (or_1_out, and_2_out, and_1_out);
  D_Flip_Flop d_ff_1 (.clk(CLK), .D(or_1_out), .Q(d_ff_1_q), .reset(CLR));  // open: Qn, preset, en
  assign Y7 = ENABLE ? d_ff_1_q : 1'bz;  // Controlled_Buffer controlled_buffer_1
  and and_3 (and_3_out, d_ff_2_q, not_1_out);
  or or_2 (or_2_out, and_3_out, and_4_out);
  and and_4 (and_4_out, X6, LOAD);
  D_Flip_Flop d_ff_2 (.clk(CLK), .D(or_2_out), .Q(d_ff_2_q), .reset(CLR));  // open: Qn, preset, en
  assign Y6 = ENABLE ? d_ff_2_q : 1'bz;  // Controlled_Buffer controlled_buffer_2
  and and_5 (and_5_out, d_ff_3_q, not_1_out);
  or or_3 (or_3_out, and_5_out, and_6_out);
  and and_6 (and_6_out, X5, LOAD);
  D_Flip_Flop d_ff_3 (.clk(CLK), .D(or_3_out), .Q(d_ff_3_q), .reset(CLR));  // open: Qn, preset, en
  and and_7 (and_7_out, d_ff_4_q, not_1_out);
  assign Y5 = ENABLE ? d_ff_3_q : 1'bz;  // Controlled_Buffer controlled_buffer_3
  and and_8 (and_8_out, X4, LOAD);
  or or_4 (or_4_out, and_7_out, and_8_out);
  D_Flip_Flop d_ff_4 (.clk(CLK), .D(or_4_out), .Q(d_ff_4_q), .reset(CLR));  // open: Qn, preset, en
  assign Y4 = ENABLE ? d_ff_4_q : 1'bz;  // Controlled_Buffer controlled_buffer_4
  and and_9 (and_9_out, d_ff_5_q, not_1_out);
  or or_5 (or_5_out, and_9_out, and_10_out);
  and and_10 (and_10_out, X3, LOAD);
  D_Flip_Flop d_ff_5 (.clk(CLK), .D(or_5_out), .Q(d_ff_5_q), .reset(CLR));  // open: Qn, preset, en
  assign Y3 = ENABLE ? d_ff_5_q : 1'bz;  // Controlled_Buffer controlled_buffer_5
  and and_11 (and_11_out, d_ff_6_q, not_1_out);
  or or_6 (or_6_out, and_11_out, and_12_out);
  and and_12 (and_12_out, X2, LOAD);
  D_Flip_Flop d_ff_6 (.clk(CLK), .D(or_6_out), .Q(d_ff_6_q), .reset(CLR));  // open: Qn, preset, en
  buf and_13 (and_13_out, d_ff_7_q);  // AND_Gate
  assign Y2 = ENABLE ? d_ff_6_q : 1'bz;  // Controlled_Buffer controlled_buffer_6
  and and_14 (and_14_out, X1, LOAD);
  or or_7 (or_7_out, and_13_out, and_14_out);
  D_Flip_Flop d_ff_7 (.clk(CLK), .D(or_7_out), .Q(d_ff_7_q), .reset(CLR));  // open: Qn, preset, en
  and and_15 (and_15_out, d_ff_8_q, not_1_out);
  assign Y1 = ENABLE ? d_ff_7_q : 1'bz;  // Controlled_Buffer controlled_buffer_7
  not not_1 (not_1_out, LOAD);
  and and_16 (and_16_out, X0, LOAD);
  or or_8 (or_8_out, and_15_out, and_16_out);
  D_Flip_Flop d_ff_8 (.clk(CLK), .D(or_8_out), .Q(d_ff_8_q), .reset(CLR));  // open: Qn, preset, en
  assign Y0 = ENABLE ? d_ff_8_q : 1'bz;  // Controlled_Buffer controlled_buffer_8

  // Notes on the sheet:
  //   Roll: 1607048
endmodule

module ALU (
  input  [7:0] X,
  input  [7:0] Y,
  input  Cin,
  output [7:0] S,
  output Cout
);

  wire fa_1_c, fa_2_c, fa_3_c, fa_4_c, fa_5_c, fa_6_c, fa_7_c;

  FA fa_1 (.X(X[0]), .Y(Y[0]), .Z(Cin), .S(S[0]), .C(fa_1_c));
  FA fa_2 (.X(X[1]), .Y(Y[1]), .Z(fa_1_c), .S(S[1]), .C(fa_2_c));
  FA fa_3 (.X(X[2]), .Y(Y[2]), .Z(fa_2_c), .S(S[2]), .C(fa_3_c));
  FA fa_4 (.X(X[3]), .Y(Y[3]), .Z(fa_3_c), .S(S[3]), .C(fa_4_c));
  FA fa_5 (.X(X[4]), .Y(Y[4]), .Z(fa_4_c), .S(S[4]), .C(fa_5_c));
  FA fa_6 (.X(X[5]), .Y(Y[5]), .Z(fa_5_c), .S(S[5]), .C(fa_6_c));
  FA fa_7 (.X(X[6]), .Y(Y[6]), .Z(fa_6_c), .S(S[6]), .C(fa_7_c));
  FA fa_8 (.X(X[7]), .Y(Y[7]), .Z(fa_7_c), .S(S[7]), .C(Cout));

  // Notes on the sheet:
  //   Faisal Ahmed
  //   Roll: 1607048
  //   X=4 (00000100)
  //   Y=8 (00001000)
endmodule
